// Logisim project 2.circ as structural Verilog: 1 circuit, main circuit instructions
module instructions (
  input  resetall,
  input  sysclock,
  output [11:0] pc,
  output [3:0] op,
  output [2:0] rd,
  output [2:0] rs1,
  output [2:0] rs2,
  output [11:0] imm
);

  Counter #(.width(12), .max('hfff)) counter_1 (
    .clr(resetall), .clk(sysclock), .Q(pc));  // open: load, up, count, D, carry
  RAM #(.addrWidth(12), .dataWidth(25)) ram_1 (
    .addr(pc), .we(1'b0), .oe(1'b1), .clk(sysclock), .data({op, rd, rs1, rs2, imm}));

  // Other names for the same wires on the sheet: clock = sysclock; reset = resetall
endmodule
