// Logisim project 4.circ as structural Verilog: 6 circuits, main circuit cpu
module cpu (
  input  resetall,
  input  sysclock,
  output [11:0] pc,
  output [11:0] x0,
  output [11:0] x1,
  output [11:0] x2,
  output [11:0] x3,
  output [11:0] x4,
  output [11:0] x5,
  output [11:0] x6,
  output [11:0] x7
);

  wire a, and_3_out, and_4_out, and_5_out, and_6_out, and_7_out, and_8_out, and_9_out, b, c, cho1, cho2, clo,
       d, halt, not_1_out, not_2_out, not_3_out, not_4_out, not_5_out, not_6_out, not_7_out, not_8_out,
       not_9_out, not_10_out, sel, stop, wen, wenwen;
  wire [2:0] destinition, rs1, rs2;
  wire [11:0] imm, multiplexer_1_out, multiplexer_2_out, multiplexer_3_out, rddata;

  Multiplexer #(.select(3), .width(12), .enable("false")) multiplexer_1 (
    .in0(x0), .in1(x1), .in2(x2), .in3(x3), .in4(x4), .in5(x5), .in6(x6), .in7(x7), .out(multiplexer_1_out),
    .sel(rs1));
  D_Flip_Flop d_ff_1 (.Qn(cho1), .preset(halt), .reset(resetall));  // open: D, clk, Q
  D_Flip_Flop d_ff_2 (.Qn(cho2), .preset(stop));  // open: D, clk, Q, reset
  Multiplexer #(.select(3), .width(12), .enable("false")) multiplexer_2 (
    .in0(x0), .in1(x1), .in2(x2), .in3(x3), .in4(x4), .in5(x5), .in6(x6), .in7(x7), .out(multiplexer_2_out),
    .sel(rs2));
  Multiplexer #(.width(12), .enable("false")) multiplexer_3 (
    .in0(multiplexer_2_out), .in1(imm), .out(multiplexer_3_out), .sel(sel));
  and and_1 (clo, sysclock, cho2);
  and and_2 (wenwen, wen, cho1, cho2);
  not not_1 (not_1_out, b);
  not not_2 (not_2_out, c);
  not not_3 (not_3_out, b);
  not not_4 (not_4_out, d);
  alu8 alu8_1 (.a(multiplexer_1_out), .b(multiplexer_3_out), .op({a, b, c, d}), .sysclock(clo), .alur(rddata));
  and and_3 (and_3_out, a, not_1_out, not_2_out);
  and and_4 (and_4_out, a, not_3_out, not_4_out);
  not not_5 (not_5_out, a);
  not not_6 (not_6_out, a);
  not not_7 (not_7_out, a);
  not not_8 (not_8_out, b);
  not not_9 (not_9_out, c);
  or or_1 (sel, and_3_out, and_4_out);
  and and_5 (and_5_out, not_5_out, d);
  and and_6 (and_6_out, not_6_out, c);
  and and_7 (and_7_out, not_7_out, b);
  and and_8 (and_8_out, not_8_out, a);
  and and_9 (and_9_out, not_9_out, a);
  instructions instructions_1 (
    .resetall(resetall), .sysclock(clo), .pc(pc), .op({a, b, c, d}), .rd(destinition), .rs1(rs1), .rs2(rs2),
    .imm(imm));  // open: jmp, a
  or or_2 (wen, and_5_out, and_6_out, and_7_out, and_8_out, and_9_out);
  // regfile regfile_1: pin names not known; wires that end beside it: rddata, pc, imm, {a, b, c, d}, wenwen, resetall, 1'b1, destinition, x0, x1, x2, x3, x4, x5, x6, x7
  not not_10 (not_10_out, d);
  and and_10 (halt, a, b, c, not_10_out);
  and and_11 (stop, a, b, c, d);

  // Other names for the same wires on the sheet: opcode[3:0] = {a, b, c, d}; reset = resetall
endmodule

module claaa (
  input  [5:0] in_1,
  input  [5:0] in_2,
  input  in_3,
  output out_4,
  output [5:0] out_5
);

  wire and_1_out, and_2_out, and_3_out, and_4_out, and_5_out, and_6_out, and_7_out, and_8_out, and_9_out,
       and_10_out, and_11_out, and_12_out, and_19_out, and_20_out, and_21_out, and_22_out, and_23_out,
       and_24_out, and_25_out, and_26_out, and_27_out, C1, C2, C3, C4, C5, G1, G2, G3, G4, G5, G6, P1, P2,
       P3, P4, P5, P6;

  and and_1 (and_1_out, in_3, P1);
  and and_2 (and_2_out, in_3, P1, P2);
  and and_3 (and_3_out, G1, P2);
  and and_4 (and_4_out, in_3, P1, P2, P3);
  and and_5 (and_5_out, G1, P2, P3);
  and and_6 (and_6_out, G2, P3);
  and and_7 (and_7_out, in_3, P1, P2, P3, P4, P5, P6);
  and and_8 (and_8_out, G1, P2, P3, P4, P5, P6);
  and and_9 (and_9_out, G2, P3, P4, P5, P6);
  and and_10 (and_10_out, G3, P4, P5, P6);
  and and_11 (and_11_out, G4, P5, P6);
  and and_12 (and_12_out, G5, P6);
  and and_13 (G1, in_1[0], in_2[0]);
  xor xor_1 (P1, in_1[0], in_2[0]);
  and and_14 (G2, in_1[1], in_2[1]);
  xor xor_2 (P2, in_1[1], in_2[1]);
  and and_15 (G3, in_1[2], in_2[2]);
  xor xor_3 (P3, in_1[2], in_2[2]);
  or or_1 (C1, and_1_out, G1);
  or or_2 (C2, and_2_out, and_3_out, G2);
  or or_3 (C3, and_4_out, and_5_out, and_6_out, G3);
  or or_4 (out_4, and_7_out, and_8_out, and_9_out, and_10_out, and_11_out, and_12_out, G6);
  and and_16 (G4, in_1[3], in_2[3]);
  xor xor_4 (P4, in_1[3], in_2[3]);
  and and_17 (G5, in_1[4], in_2[4]);
  xor xor_5 (P5, in_1[4], in_2[4]);
  and and_18 (G6, in_1[5], in_2[5]);
  xor xor_6 (P6, in_1[5], in_2[5]);
  and and_19 (and_19_out, in_3, P1, P2, P3, P4);
  and and_20 (and_20_out, G1, P2, P3, P4);
  and and_21 (and_21_out, G2, P3, P4);
  and and_22 (and_22_out, G3, P4);
  and and_23 (and_23_out, in_3, P1, P2, P3, P4, P5);
  and and_24 (and_24_out, G1, P2, P3, P4, P5);
  and and_25 (and_25_out, G2, P3, P4, P5);
  and and_26 (and_26_out, G3, P4, P5);
  and and_27 (and_27_out, G4, P5);
  or or_5 (C4, and_19_out, and_20_out, and_21_out, and_22_out, G4);
  or or_6 (C5, and_23_out, and_24_out, and_25_out, and_26_out, and_27_out, G5);
  xor xor_7 (out_5[0], in_3, P1);
  xor xor_8 (out_5[1], C1, P2);
  xor xor_9 (out_5[2], C2, P3);
  xor xor_10 (out_5[3], C3, P4);
  xor xor_11 (out_5[4], C4, P5);
  xor xor_12 (out_5[5], C5, P6);

  // Other names for the same wires on the sheet: A[5:0] = in_1; A1 = in_1[0]; A2 = in_1[1]; A3 = in_1[2];
  //   A4 = in_1[3]; A5 = in_1[4]; A6 = in_1[5]; B[5:0] = in_2; B1 = in_2[0]; B2 = in_2[1]; B3 = in_2[2]; B4 = in_2[3];
  //   B5 = in_2[4]; B6 = in_2[5]; C0 = in_3; C6 = out_4; S[5:0] = out_5; S1 = out_5[0]; S2 = out_5[1]; S3 = out_5[2];
  //   S4 = out_5[3]; S5 = out_5[4]; S6 = out_5[5]
endmodule

module alu8 (
  input  [11:0] a,
  input  [11:0] b,
  input  [3:0] op,
  input  sysclock,
  output [11:0] alur
);

  wire C0, C1, C2, claaa_1_out_4, claaa_2_out_4, O1, O2, xnor_2_out, xnor_3_out, xor_13_out, xor_14_out;
  wire [0:0] MUX1010;
  wire [2:0] MUX0111;
  wire [5:0] dif16, dif712, not_2_out, not_3_out;
  wire [11:0] MUX0000, MUX0001, MUX0010, MUX0011, MUX0100, MUX1000, MUX1011, Rresult, xnor_1_out;

  assign MUX0000 = ~a;  // NOT_Gate not_1, 12 bits wide
  assign not_2_out = ~b[5:0];  // NOT_Gate not_2, 6 bits wide
  and and_1 (MUX0001[0], a[0], b[0]);
  and and_2 (MUX0001[2], a[2], b[2]);
  and and_3 (MUX0001[1], a[1], b[1]);
  and and_4 (MUX0001[8], b[8], a[8]);
  and and_5 (MUX0001[9], a[9], b[9]);
  and and_6 (MUX0001[10], a[10], b[10]);
  and and_7 (MUX0001[11], a[11], b[11]);
  and and_8 (MUX0001[3], a[3], b[3]);
  claaa claaa_1 (.in_1(a[5:0]), .in_2(b[5:0]), .in_3(1'b0), .out_4(claaa_1_out_4), .out_5(MUX0100[5:0]));
  claaa claaa_2 (.in_1(a[5:0]), .in_2(not_2_out), .in_3(1'b1), .out_4(claaa_2_out_4), .out_5(dif16));
  Multiplexer #(.select(4), .enable("false")) multiplexer_1 (
    .in0(1'b0), .in1(1'b0), .in2(1'b0), .in3(1'b0), .in4(C1), .in5(C2), .in6(1'b0), .in7(1'b0), .in8(1'b0),
    .in9(1'b0), .in10(1'b0), .in11(1'b0), .in12(1'b0), .in13(1'b0), .in14(1'b0), .in15(1'b0), .out(C0),
    .sel(op));
  and and_9 (MUX0001[5], a[5], b[5]);
  and and_10 (MUX0001[4], a[4], b[4]);
  and and_11 (MUX0001[6], a[6], b[6]);
  and and_12 (MUX0001[7], a[7], b[7]);
  assign not_3_out = ~b[11:6];  // NOT_Gate not_3, 6 bits wide
  xor xor_1 (MUX0010[0], a[0], b[0]);
  xor xor_2 (MUX0010[2], a[2], b[2]);
  xor xor_3 (MUX0010[1], a[1], b[1]);
  xor xor_4 (MUX0010[8], b[8], a[8]);
  xor xor_5 (MUX0010[9], a[9], b[9]);
  xor xor_6 (MUX0010[10], a[10], b[10]);
  xor xor_7 (MUX0010[11], a[11], b[11]);
  xor xor_8 (MUX0010[3], a[3], b[3]);
  claaa claaa_3 (.in_1(a[11:6]), .in_2(b[11:6]), .in_3(claaa_1_out_4), .out_4(C1), .out_5(MUX0100[11:6]));
  claaa claaa_4 (.in_1(a[11:6]), .in_2(not_3_out), .in_3(claaa_2_out_4), .out_4(C2), .out_5(dif712));
  nor nor_1 (MUX0111[0], Rresult[0], Rresult[1], Rresult[2], Rresult[3], Rresult[4], Rresult[5], Rresult[6], Rresult[7], Rresult[8], Rresult[9], Rresult[10], Rresult[11]);
  xor xor_9 (MUX0010[4], a[4], b[4]);
  Multiplexer #(.select(4), .width(12), .enable("false")) multiplexer_2 (
    .in0({12{1'b0}}), .in1({12{1'b0}}), .in2({12{1'b0}}), .in3({12{1'b0}}), .in4(MUX0100),
    .in5({dif712, dif16}), .in6({12{1'b0}}), .in7({12{1'b0}}), .in8({12{1'b0}}), .in9({12{1'b0}}),
    .in10({12{1'b0}}), .in11({12{1'b0}}), .in12({12{1'b0}}), .in13({12{1'b0}}), .in14({12{1'b0}}),
    .in15({12{1'b0}}), .out(Rresult), .sel(op));
  xor xor_10 (MUX0010[6], a[6], b[6]);
  xor xor_11 (MUX0010[5], a[5], b[5]);
  xor xor_12 (MUX0010[7], a[7], b[7]);
  or or_1 (MUX0011[0], a[0], b[0]);
  or or_2 (MUX0011[1], a[1], b[1]);
  Multiplexer #(.select(4), .width(12), .enable("false")) multiplexer_3 (
    .in0(MUX0000), .in1(MUX0001), .in2(MUX0010), .in3(MUX0011), .in4(MUX0100), .in5({dif712, dif16}),
    .in6(a), .in7({{9{1'b0}}, MUX0111[2], C0, MUX0111[0]}), .in8(MUX1000), .in9(b),
    .in10({{11{1'b0}}, MUX1010[0]}), .in11(MUX1011), .in12({a[10:0], 1'b0}), .in13({1'b0, a[11:1]}),
    .out(alur), .sel(op));  // open: in14, in15
  or or_3 (MUX0011[2], a[2], b[2]);
  or or_4 (MUX0011[3], a[3], b[3]);
  or or_5 (MUX0011[8], b[8], a[8]);
  or or_6 (MUX0011[9], a[9], b[9]);
  or or_7 (MUX0011[10], a[10], b[10]);
  buf or_8 (MUX0011[11], a[11]);  // OR_Gate
  or or_9 (MUX0011[4], a[4], b[4]);
  or or_10 (MUX0011[6], a[6], b[6]);
  or or_11 (MUX0011[5], a[5], b[5]);
  or or_12 (MUX0011[7], a[7], b[7]);
  assign xnor_1_out = ~(a ^ b);  // XNOR_Gate xnor_1, 12 bits wide
  and and_13 (MUX1010[0], xnor_1_out[0], xnor_1_out[1], xnor_1_out[2], xnor_1_out[3], xnor_1_out[4], xnor_1_out[5], xnor_1_out[6], xnor_1_out[7], xnor_1_out[8], xnor_1_out[9], xnor_1_out[10], xnor_1_out[11]);
  xnor xnor_2 (xnor_2_out, a[11], b[11]);
  xor xor_13 (xor_13_out, a[11], b[11]);
  Multiplexer #(.select(4), .enable("false")) multiplexer_4 (
    .in0(1'b0), .in1(1'b0), .in2(1'b0), .in3(1'b0), .in4(O1), .in5(O2), .in6(1'b0), .in7(1'b0), .in8(1'b0),
    .in9(1'b0), .in10(1'b0), .in11(1'b0), .in12(1'b0), .in13(1'b0), .in14(1'b0), .in15(1'b0),
    .out(MUX0111[2]), .sel(op));
  xor xor_14 (xor_14_out, a[11], MUX0100[11]);
  and and_14 (O2, xor_13_out, xnor_3_out);
  xnor xnor_3 (xnor_3_out, b[11], dif712[5]);
  and and_15 (O1, xnor_2_out, xor_14_out);

  // Other names for the same wires on the sheet: B1 = b[0]; B16[5:0] = b[5:0]; MUX1001[11:0] = b; B2 = b[1];
  //   B3 = b[2]; B4 = b[3]; B5 = b[4]; B6 = b[5]; B7 = b[6]; B712[5:0] = b[11:6]; B8 = b[7]; B9 = b[8]; B10 = b[9];
  //   B11 = b[10]; B12 = b[11]; BM = b[11]; clo = sysclock; sum16[5:0] = MUX0100[5:0]; sum712[5:0] = MUX0100[11:6];
  //   O100M = MUX0100[11]; MUX0101[11:0] = {dif712, dif16}; O101M = dif712[5]; Zero = MUX0111[0]; MUX0111[1] = C0;
  //   Overflow = MUX0111[2]; A1 = a[0]; A16[5:0] = a[5:0]; MUX0110[11:0] = a; MUX1100[11:1] = a[10:0]; A2 = a[1];
  //   MUX1101[10:0] = a[11:1]; A3 = a[2]; A4 = a[3]; A5 = a[4]; A6 = a[5]; A7 = a[6]; A712[5:0] = a[11:6]; A8 = a[7];
  //   A9 = a[8]; A10 = a[9]; A11 = a[10]; A12 = a[11]; AM = a[11]; opcode[3:0] = op; rddata[11:0] = alur
endmodule

module regfile (
  input  [2:0] rd,
  input  [11:0] alur,
  input  [11:0] pc,
  input  [11:0] imm,
  input  [3:0] op,
  input  wen,
  input  resetall,
  input  sysclock,
  output [11:0] x0,
  output [11:0] x1,
  output [11:0] x2,
  output [11:0] x3,
  output [11:0] x4,
  output [11:0] x5,
  output [11:0] x6,
  output [11:0] x7
);

  wire and_1_out, and_2_out, and_3_out, and_4_out, and_5_out, and_6_out, and_7_out, and_8_out,
       decoder_1_out0, decoder_1_out1, decoder_1_out2, decoder_1_out3, decoder_1_out4, decoder_1_out5,
       decoder_1_out6, decoder_1_out7;
  wire [11:0] g, imm_t;

  Decoder #(.select(3)) decoder_1 (
    .out0(decoder_1_out0), .out1(decoder_1_out1), .out2(decoder_1_out2), .out3(decoder_1_out3),
    .out4(decoder_1_out4), .out5(decoder_1_out5), .out6(decoder_1_out6), .out7(decoder_1_out7), .sel(rd));  // open: en
  and and_1 (and_1_out, decoder_1_out0, wen);
  and and_2 (and_2_out, decoder_1_out1, wen);
  and and_3 (and_3_out, decoder_1_out2, wen);
  and and_4 (and_4_out, decoder_1_out3, wen);
  and and_5 (and_5_out, decoder_1_out4, wen);
  and and_6 (and_6_out, decoder_1_out5, wen);
  and and_7 (and_7_out, decoder_1_out6, wen);
  and and_8 (and_8_out, decoder_1_out7, wen);
  Register #(.width(12)) register_1 (.D(g), .en(and_1_out), .clk(sysclock), .Q(x0), .clr(resetall));
  Register #(.width(12)) register_2 (.D(g), .en(and_2_out), .clk(sysclock), .Q(x1), .clr(resetall));
  Register #(.width(12)) register_3 (.D(g), .en(and_3_out), .clk(sysclock), .Q(x2), .clr(resetall));
  Register #(.width(12)) register_4 (.D(g), .en(and_4_out), .clk(sysclock), .Q(x3), .clr(resetall));
  Register #(.width(12)) register_5 (.D(g), .en(and_5_out), .clk(sysclock), .Q(x4), .clr(resetall));
  Register #(.width(12)) register_6 (.D(g), .en(and_6_out), .clk(sysclock), .Q(x5), .clr(resetall));
  Register #(.width(12)) register_7 (.D(g), .en(and_7_out), .clk(sysclock), .Q(x6), .clr(resetall));
  Register #(.width(12)) register_8 (.D(g), .en(and_8_out), .clk(sysclock), .Q(x7), .clr(resetall));
  plexer plexer_1 (.in_1(alur), .pc(pc), .imm(imm_t), .in_4(op), .out_5(g));

  // Other names for the same wires on the sheet: a[2:0] = rd; c = wen; clo = sysclock; d = resetall; f[11:0] = imm;
  //   opcode[3:0] = op; xx1[11:0] = x0; xx2[11:0] = x1; xx3[11:0] = x2; xx4[11:0] = x3; xx5[11:0] = x4;
  //   xx6[11:0] = x5; xx7[11:0] = x6; xx8[11:0] = x7
endmodule

module plexer (
  input  [11:0] in_1,
  input  [11:0] pc,
  input  [11:0] imm,
  input  [3:0] in_4,
  output [11:0] out_5
);

  Multiplexer #(.select(4), .width(12), .enable("false")) multiplexer_1 (
    .in0(in_1), .in1(in_1), .in2(in_1), .in3(in_1), .in4(in_1), .in5(in_1), .in6(in_1), .in7(in_1), .in8(pc),
    .in9(imm), .in10(in_1), .in11(in_1), .in12(in_1), .in13(in_1), .in14(in_1), .in15(in_1), .out(out_5),
    .sel(in_4));
endmodule

module instructions (
  input  resetall,
  input  sysclock,
  input  jmp,
  input  [11:0] a,
  output [11:0] pc,
  output [3:0] op,
  output [2:0] rd,
  output [2:0] rs1,
  output [2:0] rs2,
  output [11:0] imm
);

  wire A1, A2, A3, A4, A5, A6, A7, A8, A9, A10, A11, A12, and_1_out, and_2_out, and_3_out, and_4_out,
       and_5_out, and_6_out, and_7_out, and_8_out, and_9_out, and_10_out, and_11_out, and_12_out, and_13_out,
       and_14_out, and_15_out, and_16_out, and_17_out, and_18_out, and_19_out, and_20_out, and_21_out,
       and_22_out, d_ff_1_qn, d_ff_2_qn, d_ff_3_qn, d_ff_4_qn, d_ff_5_qn, d_ff_6_qn, d_ff_7_qn, d_ff_8_qn,
       d_ff_9_qn, d_ff_10_qn, d_ff_11_qn, not_1_out, or_1_out, or_2_out, or_3_out, or_4_out, or_5_out,
       or_6_out, or_7_out, or_8_out, or_9_out, or_10_out, or_11_out, or_12_out, xor_1_out, xor_2_out,
       xor_3_out, xor_4_out, xor_5_out, xor_6_out, xor_7_out, xor_8_out, xor_9_out, xor_10_out, xor_11_out,
       xor_12_out;

  not not_1 (not_1_out, 1'b1);
  and and_1 (and_1_out, not_1_out, d_ff_1_qn);
  and and_2 (and_2_out, and_1_out, d_ff_2_qn);
  and and_3 (and_3_out, and_2_out, d_ff_3_qn);
  and and_4 (and_4_out, and_3_out, d_ff_4_qn);
  and and_5 (and_5_out, and_4_out, d_ff_5_qn);
  and and_6 (and_6_out, and_5_out, d_ff_6_qn);
  and and_7 (and_7_out, and_6_out, d_ff_7_qn);
  and and_8 (and_8_out, and_7_out, d_ff_8_qn);
  and and_9 (and_9_out, and_8_out, d_ff_9_qn);
  and and_10 (and_10_out, and_9_out, d_ff_10_qn);
  and and_11 (and_11_out, and_10_out, d_ff_11_qn);
  Multiplexer #(.width(12), .enable("false")) multiplexer_1 (
    .in0({A12, A11, A10, A9, A8, A7, A6, A5, A4, A3, A2, A1}), .in1(a), .out(pc), .sel(jmp));
  and and_12 (and_12_out, 1'b1, A1);
  and and_13 (and_13_out, and_12_out, A2);
  and and_14 (and_14_out, and_13_out, A3);
  and and_15 (and_15_out, and_14_out, A4);
  and and_16 (and_16_out, and_15_out, A5);
  and and_17 (and_17_out, and_16_out, A6);
  and and_18 (and_18_out, and_17_out, A7);
  and and_19 (and_19_out, and_18_out, A8);
  and and_20 (and_20_out, and_19_out, A9);
  and and_21 (and_21_out, and_20_out, A10);
  and and_22 (and_22_out, and_21_out, A11);
  or or_1 (or_1_out, 1'b1, not_1_out);
  or or_2 (or_2_out, and_12_out, and_1_out);
  or or_3 (or_3_out, and_13_out, and_2_out);
  or or_4 (or_4_out, and_14_out, and_3_out);
  or or_5 (or_5_out, and_16_out, and_5_out);
  or or_6 (or_6_out, and_17_out, and_6_out);
  or or_7 (or_7_out, and_18_out, and_7_out);
  or or_8 (or_8_out, and_19_out, and_8_out);
  or or_9 (or_9_out, and_20_out, and_9_out);
  or or_10 (or_10_out, and_21_out, and_10_out);
  or or_11 (or_11_out, and_22_out, and_11_out);
  or or_12 (or_12_out, and_15_out, and_4_out);
  xor xor_1 (xor_1_out, A9, or_8_out);
  xor xor_2 (xor_2_out, A10, or_9_out);
  xor xor_3 (xor_3_out, A11, or_10_out);
  xor xor_4 (xor_4_out, A1, or_1_out);
  xor xor_5 (xor_5_out, A2, or_2_out);
  xor xor_6 (xor_6_out, A3, or_3_out);
  xor xor_7 (xor_7_out, A4, or_4_out);
  xor xor_8 (xor_8_out, A5, or_12_out);
  xor xor_9 (xor_9_out, A6, or_5_out);
  xor xor_10 (xor_10_out, A7, or_6_out);
  xor xor_11 (xor_11_out, A8, or_7_out);
  xor xor_12 (xor_12_out, A12, or_11_out);
  D_Flip_Flop d_ff_1 (.D(xor_4_out), .clk(sysclock), .Q(A1), .Qn(d_ff_1_qn), .reset(resetall));  // open: preset
  D_Flip_Flop d_ff_2 (.D(xor_5_out), .clk(sysclock), .Q(A2), .Qn(d_ff_2_qn), .reset(resetall));  // open: preset
  D_Flip_Flop d_ff_3 (.D(xor_6_out), .clk(sysclock), .Q(A3), .Qn(d_ff_3_qn), .reset(resetall));  // open: preset
  D_Flip_Flop d_ff_4 (.D(xor_7_out), .clk(sysclock), .Q(A4), .Qn(d_ff_4_qn), .reset(resetall));  // open: preset
  D_Flip_Flop d_ff_5 (.D(xor_8_out), .clk(sysclock), .Q(A5), .Qn(d_ff_5_qn), .reset(resetall));  // open: preset
  D_Flip_Flop d_ff_6 (.D(xor_9_out), .clk(sysclock), .Q(A6), .Qn(d_ff_6_qn), .reset(resetall));  // open: preset
  D_Flip_Flop d_ff_7 (.D(xor_10_out), .clk(sysclock), .Q(A7), .Qn(d_ff_7_qn), .reset(resetall));  // open: preset
  D_Flip_Flop d_ff_8 (.D(xor_11_out), .clk(sysclock), .Q(A8), .Qn(d_ff_8_qn), .reset(resetall));  // open: preset
  D_Flip_Flop d_ff_9 (.D(xor_1_out), .clk(sysclock), .Q(A9), .Qn(d_ff_9_qn), .reset(resetall));  // open: preset
  D_Flip_Flop d_ff_10 (.D(xor_2_out), .clk(sysclock), .Q(A10), .Qn(d_ff_10_qn), .reset(resetall));  // open: preset
  D_Flip_Flop d_ff_11 (.D(xor_3_out), .clk(sysclock), .Q(A11), .Qn(d_ff_11_qn), .reset(resetall));  // open: preset
  D_Flip_Flop d_ff_12 (.D(xor_12_out), .clk(sysclock), .Q(A12), .reset(resetall));  // open: Qn, preset
  RAM #(.addrWidth(12), .dataWidth(25)) ram_1 (
    .addr(pc), .we(1'b0), .oe(1'b1), .clk(sysclock), .data({op, rd, rs1, rs2, imm}));

  // Other names for the same wires on the sheet: clk = sysclock; counterO[11:0] = pc;
  //   counterO1[11:0] = {A12, A11, A10, A9, A8, A7, A6, A5, A4, A3, A2, A1}
endmodule
