// Logisim project extracredit.circ as structural Verilog: 2 circuits, main circuit ledger
module ledger (
  input  [2:0] customerid,
  input  [1:0] transactiontype,
  input  [7:0] transactionamount,
  input  sysclock,
  output [1:0] transactionresult,
  output [7:0] amountremaining
);

  wire Enable0, Enable1, Enable2, Enable3, Enable4, Enable5, Enable6, Enable7;
  wire [7:0] multiplexer_1_out, multiplexer_2_out, query1, query2, query3, query4, query5, query6, query7,
       query8;

  Register register_1 (.D(amountremaining), .en(Enable0), .clk(sysclock), .Q(query1));  // open: clr
  Register register_2 (.D(amountremaining), .en(Enable1), .clk(sysclock), .Q(query2));  // open: clr
  Register register_3 (.D(amountremaining), .en(Enable2), .clk(sysclock), .Q(query3));  // open: clr
  Register register_4 (.D(amountremaining), .en(Enable3), .clk(sysclock), .Q(query4));  // open: clr
  Register register_5 (.D(amountremaining), .en(Enable4), .clk(sysclock), .Q(query5));  // open: clr
  Register register_6 (.D(amountremaining), .en(Enable5), .clk(sysclock), .Q(query6));  // open: clr
  Register register_7 (.D(amountremaining), .en(Enable6), .clk(sysclock), .Q(query7));  // open: clr
  Register register_8 (.D(amountremaining), .en(Enable7), .clk(sysclock), .Q(query8));  // open: clr
  Decoder #(.select(3)) decoder_1 (
    .out0(Enable0), .out1(Enable1), .out2(Enable2), .out3(Enable3), .out4(Enable4), .out5(Enable5),
    .out6(Enable6), .out7(Enable7), .sel(customerid));  // open: en
  Multiplexer #(.select(3), .width(8), .enable("false")) multiplexer_1 (
    .in0(query1), .in1(query2), .in2(query3), .in3(query4), .in4(query5), .in5(query6), .in6(query7),
    .in7(query8), .out(multiplexer_1_out), .sel(customerid));
  Multiplexer #(.select(3), .width(8), .enable("false")) multiplexer_2 (
    .in0(query1), .in1(query2), .in2(query3), .in3(query4), .in4(query5), .in5(query6), .in6(query7),
    .in7(query8), .out(multiplexer_2_out), .sel(customerid));
  ALU alu_1 (
    .query(multiplexer_1_out), .transactionamount(transactionamount), .transactiontype(transactiontype),
    .transactionresult(transactionresult), .ALUout(amountremaining));

  // Other names for the same wires on the sheet: ALUout[7:0] = amountremaining
endmodule

module ALU (
  input  [7:0] query,
  input  [7:0] transactionamount,
  input  [1:0] transactiontype,
  output [1:0] transactionresult,
  output [7:0] ALUout
);

  wire adder_1_cout, comparator_1_eq, comparator_1_gt, comparator_1_lt;
  wire [1:0] Result01, Result10;
  wire [7:0] adder_1_out, ALU01, ALU10, subtractor_1_out;

  Adder adder_1 (.a(query), .b(transactionamount), .out(adder_1_out), .cout(adder_1_cout));  // open: cin
  Subtractor subtractor_1 (.a(query), .b(transactionamount), .out(subtractor_1_out));  // open: bin, bout
  Comparator #(.mode("unsigned")) comparator_1 (
    .a(query), .b(transactionamount), .gt(comparator_1_gt), .eq(comparator_1_eq), .lt(comparator_1_lt));
  Multiplexer #(.width(8), .enable("false")) multiplexer_1 (
    .in0(adder_1_out), .in1(query), .out(ALU01), .sel(adder_1_cout));
  Multiplexer #(.width(8), .enable("false")) multiplexer_2 (
    .in0(subtractor_1_out), .in1(query), .out(ALU10), .sel(comparator_1_lt));
  Multiplexer #(.width(2), .enable("false")) multiplexer_3 (
    .in0(2'b01), .in1(2'b11), .out(Result10), .sel(comparator_1_lt));
  Multiplexer #(.width(2), .enable("false")) multiplexer_4 (
    .in0(2'b01), .in1(2'b10), .out(Result01), .sel(adder_1_cout));
  Multiplexer #(.select(2), .width(8), .enable("false")) multiplexer_5 (
    .in0(query), .in1(ALU01), .in2(ALU10), .out(ALUout), .sel(transactiontype));  // open: in3
  Multiplexer #(.select(2), .width(2), .enable("false")) multiplexer_6 (
    .in0(2'b00), .in1(Result01), .in2(Result10), .out(transactionresult), .sel(transactiontype));  // open: in3

  // Other names for the same wires on the sheet: A[7:0] = query; ALU00[7:0] = query; B[7:0] = transactionamount
endmodule
